// Logisim project lab2.circ as structural Verilog: 1 circuit, main circuit main
module main (
  input  A0,
  input  A1,
  input  B0,
  input  B1,
  input  S,
  output Y0,
  output Y1
);

  wire and_1_out, and_2_out, n4_to_1_mux_x2_74153_1_p13, n4_to_1_mux_x2_74153_1_p14,
       n4_to_1_mux_x2_74153_2_p13, n4_to_1_mux_x2_74153_2_p14, not_1_out, not_2_out, not_3_out, not_4_out,
       or_1_out, xor_1_out;

  not not_1 (not_1_out, B0);
  not not_2 (not_2_out, B1);
  not not_3 (not_3_out, S);
  or or_1 (or_1_out, B0, B1);
  xor xor_1 (xor_1_out, B0, B1);
  not not_4 (not_4_out, xor_1_out);
  and and_1 (and_1_out, B0, not_2_out);
  and and_2 (and_2_out, not_1_out, B1);
  // _4_to_1_MUX__x2___74153 #(.Facing("east")) 4_to_1_mux_x2_74153_1: pin names not known; wires that end beside it: 1'b0, or_1_out, and_1_out, B0, 1'b0, 1'b0, B1, B1, S, A0, S, A1, n4_to_1_mux_x2_74153_1_p13, n4_to_1_mux_x2_74153_1_p14
  // _4_to_1_MUX__x2___74153 #(.Facing("east")) 4_to_1_mux_x2_74153_2: pin names not known; wires that end beside it: and_1_out, not_4_out, and_2_out, and_1_out, and_2_out, and_1_out, not_4_out, and_2_out, not_3_out, A0, not_3_out, A1, n4_to_1_mux_x2_74153_2_p13, n4_to_1_mux_x2_74153_2_p14
  or or_2 (Y0, n4_to_1_mux_x2_74153_1_p13, n4_to_1_mux_x2_74153_2_p13);
  or or_3 (Y1, n4_to_1_mux_x2_74153_1_p14, n4_to_1_mux_x2_74153_2_p14);
endmodule
